# Fritzing sketch alarmOverflowingLiquid (saved by Fritzing 0.9.2b)
breadboards: 1

parts:
  Arduino1 = Arduino Uno (Rev3)
  Parte3 = Humidity Sensor - HIH-4030 Breakout

nets:
  N1: Arduino1.A0, Parte3.OUT
  GND: Arduino1.GND, Parte3.GND
  5V: Arduino1.5V, Parte3.VCC

notes:
  When water overcomes the middle of the water sensor a LED blinks, if not the LED is OFF.
  Applications: Based on a maxim level, checks if a liquid is overflowing it and an alarm sounds. For example air aconditioner.
  https://github.com/adgellida/arduinoProjects/tree/master/alarmOverflowingLiquid
