# Fritzing sketch bionicFinger (saved by Fritzing 0.9.2b)
breadboards: 1

parts:
  Arduino1 = Arduino Uno (Rev3)
  LED1 = smd LED [color="Red (633nm)" package="1206 [SMD]"]
  R1 = Resistor [tolerance=±5% resistance=220 package="0603 [SMD]"]
  LCD2 = LCD screen
  S1 = Pushbutton [package="[SMD]"]
  R3 = Resistor [tolerance=±5% resistance=10k package="0603 [SMD]"]
  S2 = Pushbutton [package="[SMD]"]
  R5 = Trimmer Potentiometer [maximum_resistance=4.7kΩ package=THT]
  R4 = Resistor [tolerance=±5% resistance=10k package="0603 [SMD]"]
  R6 = Resistor [tolerance=±5% resistance=10k package="0603 [SMD]"]

nets:
  N1: Arduino1.D11_PWM/MOSI, LCD2.E
  N2: Arduino1.D12/MISO, LCD2.RS
  N3: Arduino1.D13/SCK, LED1.anode
  GND: Arduino1.GND, R1.Pin_1, LCD2.VSS, LCD2.R/W, LCD2.LED-, R3.Pin_1, R5.leg2, R4.Pin_1
  N4: Arduino1.D2, LCD2.DB7
  N5: Arduino1.D3_PWM, LCD2.DB6
  N6: Arduino1.D4, LCD2.DB5
  N7: Arduino1.D5_PWM, LCD2.DB4
  N8: Arduino1.D6_PWM, S1.Pin_3, S1.Pin_4, R3.Pin_0
  N9: Arduino1.D7, S2.Pin_3, S2.Pin_4, R4.Pin_0
  5V: Arduino1.5V, LCD2.VDD, S1.Pin_1, S1.Pin_2, S2.Pin_1, S2.Pin_2, R5.leg1, R6.Pin_1
  N10: LED1.cathode, R1.Pin_0
  N11: LCD2.V0, R5.wiper
  N12: LCD2.LED+, R6.Pin_0

notes:
  Touch the button repeately to score high!
  Applications: Games.
  https://github.com/adgellida/arduinoProjects/tree/master/bionicFinger
