# Fritzing sketch irCommunication (saved by Fritzing 0.9.2b)
breadboards: 1

parts:
  Arduino1 = Arduino Uno (Rev3)
  IR1 = TSOP312.., 314.. [package=THT]
  LED1 = smd LED [color="Red (633nm)" package="1206 [SMD]"]
  LED3 = LEDs [package=led10mm]
  R1 = Resistor [tolerance=±5% resistance=220 package="0603 [SMD]"]
  R2 = Resistor [tolerance=±5% resistance=220 package="0603 [SMD]"]

nets:
  GND: Arduino1.GND, IR1.GND, LED1.cathode, LED3.A
  N1: Arduino1.D2, R2.Pin_1
  N2: Arduino1.D3_PWM, R1.Pin_1
  N3: Arduino1.D4, IR1.Data
  N4: Arduino1.5V, IR1.Vs
  N5: LED1.anode, R1.Pin_0
  N6: LED3.C, R2.Pin_0

notes:
  Push IR remote buttons to do actions!
  If you push button 2 a LED turns ON, if you push another time it turns OFF.
  Do the same with button 3.
  It doesn't work perfect but is very functional.
  Applications: You can connect outputs to anything and you control them with an IR remote control.
  https://github.com/adgellida/arduinoProjects/tree/master/irCommunication
