# Fritzing sketch powerOffMonitorBasedOnPresence (saved by Fritzing 0.9.2b)
breadboards: 1

parts:
  Arduino1 = Arduino Uno (Rev3)
  PIR1 = PIR sensor

nets:
  N1: Arduino1.A0, PIR1.SIG
  5V: Arduino1.5V, PIR1.VDD
  GND: Arduino1.GND, PIR1.GND

notes:
  Power off your monitor if you go away from your desk and power on if you return.
  For now if sensor detects you blinks a LED for 2-3 seconds aprox.
  https://github.com/adgellida/arduinoProjects/tree/master/powerOffMonitorBasedOnPresence
